# Fritzing sketch ir_sensor (saved by Fritzing 0.9.3b)
breadboards: 1

parts:
  부품1 = Arduino Uno (Rev3) - ICSP
  LED2 = LED - 5mm [color="Yellow (595nm)" package="5 mm [THT]"]
  R2 = Resistor [tolerance=±5% resistance=220 package=THT]
  M1 = fc-51 [package=THT]

nets:
  N1: 부품1.D8, R2.Pin_0
  N2: 부품1.D2, M1.pin1
  N3: 부품1.5V, LED2.cathode, M1.pin3
  N4: 부품1.GND, M1.pin2
  N5: LED2.anode, R2.Pin_1
