# Fritzing sketch lcd1602_control (saved by Fritzing 0.9.3b)
breadboards: 1

parts:
  부품1 = Arduino Uno (Rev3) - ICSP
  R2 = Resistor [tolerance=±5% resistance=220 package=THT]
  LCD1 = LCD screen
  Display1 = LCD screen 16x2 IIC [part_number=101290]
  R3 = Rotary Potentiometer (Small) [maximum_resistance=100kΩ package=THT]

nets:
  N1: 부품1.A4/SDA, Display1.SDA
  N2: 부품1.A5/SCL, Display1.SCL
  5V: 부품1.5V, R2.Pin_0, LCD1.VDD, Display1.VCC, R3.leg2
  GND: 부품1.GND, LCD1.VSS, LCD1.R/W, LCD1.LED-, Display1.GND, R3.leg1
  N3: 부품1.D8, LCD1.DB4
  N4: 부품1.D9_PWM, LCD1.DB5
  N5: 부품1.D10_PWM/SS, LCD1.DB6
  N6: 부품1.D11_PWM/MOSI, LCD1.DB7
  N7: 부품1.D4, LCD1.RS
  N8: 부품1.D5_PWM, LCD1.E
  N9: R2.Pin_1, LCD1.LED+
  N10: LCD1.V0, R3.wiper

custom parts:
  LCD screen 16x2 IIC: LCD screen with HD44780 controller enables showing text, symbols, value or anything else that comes from Croduino/Arduino. It is capable of showing 16 symbols in two lines and therefore can be used in many projects that need to send clearly visible and legible output information.. • Color of symbols: White • Backlight: Blue • Dimensions: 80 x 36 x 12 mm • Screen dimensions: 64.5 x 16 mm •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
