# Fritzing sketch led_analogWrite (saved by Fritzing 0.9.3b)
breadboards: 1

parts:
  부품1 = Arduino Uno (Rev3)
  LED1 = LED - 5mm [color="Red (633nm)" package="5 mm [THT]"]
  LED2 = LED - 5mm [color="Yellow (595nm)" package="5 mm [THT]"]
  LED3 = LED - 5mm [color="Green (570nm)" package="5 mm [THT]"]
  R1 = Resistor [tolerance=±5% resistance=220 package="0603 [SMD]"]
  R2 = Resistor [tolerance=±5% resistance=220 package="0603 [SMD]"]
  R3 = Resistor [tolerance=±5% resistance=220 package="0603 [SMD]"]
  R4 = Rotary Potentiometer (Small) [maximum_resistance=100kΩ package=THT]
  R5 = Rotary Potentiometer (Small) [maximum_resistance=100kΩ package=THT]

nets:
  N1: 부품1.A0, R4.wiper
  N2: 부품1.A1, R5.wiper
  N3: 부품1.D9_PWM, R3.Pin_0
  N4: 부품1.D10_PWM/SS, R2.Pin_0
  N5: 부품1.D11_PWM/MOSI, R1.Pin_0
  N6: 부품1.GND, LED1.cathode, LED2.cathode, LED3.cathode, R4.leg2, R5.leg1
  N7: 부품1.5V, R4.leg1, R5.leg2
  N8: LED1.anode, R3.Pin_1
  N9: LED2.anode, R2.Pin_1
  N10: LED3.anode, R1.Pin_1
