# Fritzing sketch photo_resistor (saved by Fritzing 0.9.3b)
breadboards: 1

parts:
  부품1 = Arduino Uno (Rev3) - ICSP
  LED1 = LED - 5mm [color="Red (633nm)" package="5 mm [THT]"]
  LED3 = LED - 5mm [color="Green (570nm)" package="5 mm [THT]"]
  R1 = Resistor [tolerance=±5% resistance=220 package=THT]
  R2 = Resistor [tolerance=±5% resistance=10k package=THT]
  R3 = Resistor [tolerance=±5% resistance=220 package=THT]
  R4 = PHOTOCELL [package=photocell]
  R5 = PHOTOCELL [package=photocell]
  R6 = Resistor [tolerance=±5% resistance=10k package=THT]

nets:
  N1: 부품1.A0, R5.P$2, R6.Pin_1
  N2: 부품1.A1, R2.Pin_0, R4.P$1
  N3: 부품1.5V, LED1.cathode, LED3.cathode, R2.Pin_1, R5.P$1
  N4: 부품1.D9_PWM, R3.Pin_0
  N5: 부품1.D10_PWM/SS, R1.Pin_0
  N6: 부품1.GND, R4.P$2, R6.Pin_0
  N7: LED1.anode, R3.Pin_1
  N8: LED3.anode, R1.Pin_1
