# Fritzing sketch rgb_led_analogWrite (saved by Fritzing 0.9.3b)
breadboards: 1

parts:
  부품1 = Arduino Uno (Rev3)
  R1 = Resistor [tolerance=±5% resistance=220 package="0603 [SMD]"]
  R4 = Rotary Potentiometer (Small) [maximum_resistance=100kΩ package=THT]
  R5 = Rotary Potentiometer (Small) [maximum_resistance=100kΩ package=THT]
  LED4 = RGB LED (com. cathode, rgb) [package="5 mm [THT]"]
  R6 = Rotary Potentiometer (Small) [maximum_resistance=100kΩ package=THT]
  S1 = Pushbutton [package="[THT]"]

nets:
  N1: 부품1.A0, R4.wiper
  N2: 부품1.A1, R5.wiper
  N3: 부품1.A2, R6.wiper
  N4: 부품1.D9_PWM, LED4.blue_anode
  N5: 부품1.D10_PWM/SS, LED4.green_anode
  N6: 부품1.D11_PWM/MOSI, LED4.red_anode
  N7: 부품1.D2, S1.Pin_3, S1.Pin_4
  N8: 부품1.5V, R4.leg1, R5.leg1, R6.leg1
  N9: 부품1.GND, R1.Pin_1, R4.leg2, R5.leg2, R6.leg2, S1.Pin_1, S1.Pin_2
  N10: R1.Pin_0, LED4.common_cathode
