# Fritzing sketch servo_control (saved by Fritzing 0.9.3b)
breadboards: 1

parts:
  부품1 = Arduino Uno (Rev3)
  VCC1 = 4 x AAA Battery Mount
  servoA(180_degree) = Basic Servo
  servoB(180_degree) = Basic Servo
  servoC(360_degree) = Basic Servo

nets:
  N1: 부품1.D9_PWM, servoA(180_degree).pulse
  N2: 부품1.D10_PWM/SS, servoB(180_degree).pulse
  N3: 부품1.D11_PWM/MOSI, servoC(360_degree).pulse
  GND: 부품1.GND, VCC1.-, servoA(180_degree).gnd, servoB(180_degree).gnd, servoC(360_degree).gnd
  VCC: VCC1.+, servoA(180_degree).vcc, servoB(180_degree).vcc, servoC(360_degree).vcc
