# Fritzing sketch seven_segment_display (saved by Fritzing 0.9.3b)
breadboards: 1

parts:
  부품1 = Arduino Uno (Rev3) - ICSP
  R1 = Resistor [tolerance=±5% resistance=330 package=THT]
  R2 = Resistor [tolerance=±5% resistance=330 package=THT]
  7_Segment2 = 7 Segment Display

nets:
  N1: 부품1.D8, 7_Segment2.Segment_G
  N2: 부품1.D9_PWM, 7_Segment2.Segment_DP
  N3: 부품1.D2, 7_Segment2.Segment_A
  N4: 부품1.D3_PWM, 7_Segment2.Segment_B
  N5: 부품1.D4, 7_Segment2.Segment_C
  N6: 부품1.D5_PWM, 7_Segment2.Segment_D
  N7: 부품1.D6_PWM, 7_Segment2.Segment_E
  N8: 부품1.D7, 7_Segment2.Segment_F
  N9: 부품1.GND, R1.Pin_1, R2.Pin_0
  N10: R1.Pin_0, 7_Segment2.common_cathode#8
  N11: R2.Pin_1, 7_Segment2.common_cathode#3

custom parts:
  7 Segment Display: 7 Segment Display with common cathode.
