# Fritzing sketch ultrasonic_sensor (saved by Fritzing 0.9.3b)
breadboards: 1

parts:
  부품1 = Arduino Uno (Rev3) - ICSP
  hc-sr1 = hc-sr04

nets:
  N1: 부품1.D8, hc-sr1.Echo
  N2: 부품1.D9_PWM, hc-sr1.Trig
  5V: 부품1.5V, hc-sr1.VCC
  GND: 부품1.GND, hc-sr1.GND
