# Fritzing sketch led_button_potentiometer (saved by Fritzing 0.9.3b)
breadboards: 1

parts:
  부품1 = Arduino Uno (Rev3) - ICSP
  LED1 = LED - 5mm [color="Red (633nm)" package="5 mm [THT]"]
  LED2 = LED - 5mm [color="Yellow (595nm)" package="5 mm [THT]"]
  LED3 = LED - 5mm [color="Green (570nm)" package="5 mm [THT]"]
  R5 = Rotary Potentiometer (Small) [maximum_resistance=100kΩ package=THT]
  R1 = Resistor [tolerance=±5% resistance=220 package=THT]
  LED4 = LED - 5mm [color="Blue (430nm)" package="5 mm [THT]"]
  LED5 = LED - 5mm [color="Orange (605nm)" package="5 mm [THT]"]
  R6 = Resistor [tolerance=±5% resistance=220 package=THT]
  R7 = Resistor [tolerance=±5% resistance=220 package=THT]
  R8 = Resistor [tolerance=±5% resistance=220 package=THT]
  R9 = Resistor [tolerance=±5% resistance=220 package=THT]
  S1 = Pushbutton [package="[THT]"]
  S2 = Pushbutton [package="[THT]"]

nets:
  N1: 부품1.A0, R5.wiper
  N2: 부품1.ICSP_MOSI, 부품1.D11_PWM/MOSI, LED1.anode
  N3: 부품1.D9_PWM, LED3.anode
  N4: 부품1.D10_PWM/SS, LED2.anode
  N5: 부품1.D2, S2.Pin_1, S2.Pin_2
  N6: 부품1.D3_PWM, S1.Pin_1, S1.Pin_2
  N7: 부품1.D5_PWM, LED5.anode
  N8: 부품1.D6_PWM, LED4.anode
  N9: 부품1.5V, R5.leg1
  N10: 부품1.GND, R5.leg2, R1.Pin_0, R6.Pin_0, R7.Pin_0, R8.Pin_0, R9.Pin_0, S1.Pin_3, S1.Pin_4, S2.Pin_3, S2.Pin_4
  N11: LED1.cathode, R1.Pin_1
  N12: LED2.cathode, R6.Pin_1
  N13: LED3.cathode, R7.Pin_1
  N14: LED4.cathode, R8.Pin_1
  N15: LED5.cathode, R9.Pin_1
