# Fritzing sketch seven_segment_button (saved by Fritzing 0.9.3b)
breadboards: 1

parts:
  부품1 = Arduino Uno (Rev3) - ICSP
  R1 = Resistor [tolerance=±5% resistance=330 package=THT]
  R2 = Resistor [tolerance=±5% resistance=330 package=THT]
  7_Segment2 = 7 Segment Display
  S1 = Pushbutton [package="[THT]"]
  S2 = Pushbutton [package="[THT]"]

nets:
  N1: 부품1.D8, 7_Segment2.Segment_G
  N2: 부품1.D10_PWM/SS, S1.Pin_3, S1.Pin_4
  N3: 부품1.D11_PWM/MOSI, S2.Pin_3, S2.Pin_4
  N4: 부품1.D2, 7_Segment2.Segment_A
  N5: 부품1.D3_PWM, 7_Segment2.Segment_B
  N6: 부품1.D4, 7_Segment2.Segment_C
  N7: 부품1.D5_PWM, 7_Segment2.Segment_D
  N8: 부품1.D6_PWM, 7_Segment2.Segment_E
  N9: 부품1.D7, 7_Segment2.Segment_F
  N10: 부품1.GND, R1.Pin_1, R2.Pin_0, S1.Pin_1, S1.Pin_2, S2.Pin_1, S2.Pin_2
  N11: R1.Pin_0, 7_Segment2.common_cathode#8
  N12: R2.Pin_1, 7_Segment2.common_cathode#3

custom parts:
  7 Segment Display: 7 Segment Display with common cathode.
